# Fritzing sketch sensor_sole (saved by Fritzing 0.9.2b)
circuit board: 8.46667cm x 5.64444cm
breadboards: 1

parts:
  RFduino1 = RFduino SMD
  J1 = female pin header, 6 pins [form="♀ (female)"]
  J2 = female pin header, 6 pins [form="♀ (female)"]
  R1 = Resistor [tolerance=±5% resistance=1k package=THT]
  R2 = Resistor [tolerance=±5% resistance=1k package=THT]
  R3 = Resistor [tolerance=±5% resistance=1k package=THT]
  R4 = Resistor [tolerance=±5% resistance=1k package=THT]
  R5 = Resistor [tolerance=±5% resistance=1k package=THT]
  R6 = Resistor [tolerance=±5% resistance=1k package=THT]

nets:
  N1: RFduino1.gnd, R1.Pin_1, R2.Pin_1, R3.Pin_1, R4.Pin_1, R5.Pin_1, R6.Pin_1
  N2: RFduino1.vin, J1.pin1, J1.pin2, J1.pin3, J1.pin4, J1.pin5, J1.pin6
  N3: RFduino1.gpio1, J2.pin1, R4.Pin_0
  N4: RFduino1.gpio2, J2.pin2, R5.Pin_0
  N5: RFduino1.gpio3, J2.pin3, R6.Pin_0
  N6: RFduino1.gpio4, J2.pin4, R1.Pin_0
  N7: RFduino1.gpio5, J2.pin5, R2.Pin_0
  N8: RFduino1.gpio6, J2.pin6, R3.Pin_0

custom parts:
  RFduino SMD: RFduino board
